// Logisim project practicWork2MUX_2_to_1.circ as structural Verilog: 1 circuit, main circuit main
module main (
  input  D0,
  input  Sel,
  input  D1,
  output out_4
);

  wire and_1_out, and_2_out, not_1_out;

  not not_1 (not_1_out, Sel);
  and and_1 (and_1_out, D0, Sel);
  and and_2 (and_2_out, D1, not_1_out);
  or or_1 (out_4, and_1_out, and_2_out);
endmodule
