// Logisim project practicWork2fullAdder.circ as structural Verilog: 1 circuit, main circuit main
module main (
  input  A,
  input  B,
  input  Cin,
  output Sum,
  output Count
);

  wire and_1_out, and_2_out, xor_1_out;

  xor xor_1 (xor_1_out, A, B);
  and and_1 (and_1_out, B, A);
  and and_2 (and_2_out, xor_1_out, B, B);
  xor xor_2 (Sum, xor_1_out, and_1_out);
  or or_1 (Count, and_1_out, and_2_out);

  assign Cin = B;
endmodule
